# Fritzing sketch Schematic-Photocell (saved by Fritzing 0.9.3b)
breadboards: 1

parts:
  Part1 = Arduino Uno (Rev3)
  LED1 = LED - 5mm [color="Red (633nm)" package="5 mm [THT]"]
  R1 = Photocell (LDR) [package=THT]
  R2 = Resistor [tolerance=±5% resistance=5.6k package=THT]

nets:
  N1: Part1.A0, R1.pin_0, R2.Pin_0
  N2: Part1.D9_PWM, LED1.anode
  N3: Part1.5V, R2.Pin_1
  N4: Part1.GND, LED1.cathode, R1.pin_1
