# Fritzing sketch Schematic-VideoGeneration (saved by Fritzing 0.9.3b)
breadboards: 1

parts:
  Part1 = Arduino Uno (Rev3)
  JP1 = RCA [package=rca_lock]
  R2 = Resistor [tolerance=±5% resistance=1k package=THT]
  R3 = Resistor [tolerance=±5% resistance=470 package=THT]
  JP2 = RCA [package=rca_lock]

nets:
  N1: Part1.D9_PWM, R2.Pin_0
  N2: Part1.D7, R3.Pin_0
  N3: JP1.SWITCH, JP2.SWITCH
  N4: R2.Pin_1, R3.Pin_1
