# Fritzing sketch Schematic-ALL (saved by Fritzing 0.9.3b)
breadboards: 1

parts:
  Part1 = Arduino Uno (Rev3)
  S1 = Pushbutton [package="[THT]"]
  LED2 = LED - 5mm [color="Red (633nm)" package="5 mm [THT]"]
  LED1 = LED - 5mm [color="Red (633nm)" package="5 mm [THT]"]
  S2 = Pushbutton [package="[THT]"]  # not connected

nets:
  N1: Part1.D9_PWM, LED1.anode
  N2: Part1.D13/SCK, LED2.anode
  N3: Part1.GND, S1.Pin_3, S1.Pin_4, LED2.cathode, LED1.cathode
