# Fritzing sketch Schematic-DCMotor (saved by Fritzing 0.9.3b)
breadboards: 1

parts:
  Part1 = Arduino Uno (Rev3)
  M1 = DC Motor
  D1 = Rectifier Diode [part_number=1N4001 package="300 mil [THT]"]
  R1 = Resistor [tolerance=±5% resistance=270 package=THT]
  Q1 = NPN-Transistor [package="TO92 [THT]"]

nets:
  N1: Part1.D9_PWM, R1.Pin_0
  N2: Part1.5V, M1.pin_2, D1.cathode
  N3: Part1.GND, Q1.E
  N4: M1.pin_1, D1.anode, Q1.C
  N5: R1.Pin_1, Q1.B
