# Fritzing sketch FritzingDemo (saved by Fritzing 0.9.3b)
circuit board: 3.8cm x 3.3cm
breadboards: 1

parts:
  ATtiny85 = attiny85 [package=dip]
  LED = LED - 5mm [color="Red (633nm)" package="5 mm [THT]"]
  DOWN = Pushbutton [package="[THT]"]
  UP = Pushbutton [package="[THT]"]
  +5V = male pin header, 2 pins [form="♂ (male)"]

nets:
  N1: ATtiny85.Pin_4, LED.cathode, DOWN.Pin_3, DOWN.Pin_4, UP.Pin_3, UP.Pin_4, +5V.pin2
  N2: ATtiny85.Pin_5, LED.anode
  N3: ATtiny85.Pin_6, UP.Pin_1, UP.Pin_2
  N4: ATtiny85.Pin_7, DOWN.Pin_1, DOWN.Pin_2
  N5: ATtiny85.Pin_8, +5V.pin1

notes:
  ~D0
  ~D1
  D2/A1
  power in
  METRO-
  -NOME
